// Logisim project schematic.circ as structural Verilog: 1 circuit, main circuit main
module main (
  input  [31:0] a,
  input  [31:0] b,
  input  sub_notadd,
  output [31:0] s,
  output cout
);

  wire [31:0] multiplexer_1_out, not_1_out;

  assign not_1_out = ~b;  // NOT_Gate not_1, 32 bits wide
  Multiplexer #(.width(32)) multiplexer_1 (.in0(b), .in1(not_1_out), .out(multiplexer_1_out), .sel(sub_notadd));
  Adder #(.width(32)) adder_1 (.a(a), .b(multiplexer_1_out), .out(s), .cin(sub_notadd), .cout(cout));
endmodule
