// Logisim project RTL.circ as structural Verilog: 1 circuit, main circuit main
module main (
  input  [31:0] in1,
  input  load,
  input  clk,
  output [31:0] out1
);

  wire decoder_1_out0, decoder_1_out1, decoder_1_out2, decoder_1_out3, or_1_out, or_2_out;
  wire [1:0] stateCounter_q;
  wire [31:0] multiplexer_1_out, multiplexer_2_out, multiplexer_3_out, negator_1_out, R1_q, shifter_1_out,
       xor_1_out;

  Counter #(.max('h3), .width(2)) stateCounter (
    .clr(load), .load(1'b0), .up(1'b1), .clk(clk), .Q(stateCounter_q));  // open: count, D, carry
  Shifter #(.width(32)) shifter_1 (.in(R1_q), .\dist (5'b00001), .out(shifter_1_out));
  or or_1 (or_1_out, load, decoder_1_out1);
  Register #(.width(32)) R1 (.D(multiplexer_1_out), .en(or_1_out), .clk(clk), .Q(R1_q));  // open: clr
  Multiplexer #(.width(32)) multiplexer_1 (.in0(shifter_1_out), .in1(in1), .out(multiplexer_1_out), .sel(load));
  Decoder #(.enable("false"), .select(2)) decoder_1 (
    .out0(decoder_1_out0), .out1(decoder_1_out1), .out2(decoder_1_out2), .out3(decoder_1_out3),
    .sel(stateCounter_q));
  assign xor_1_out = R1_q ^ out1;  // XOR_Gate xor_1, 32 bits wide
  Multiplexer #(.width(32)) multiplexer_2 (.in0(xor_1_out), .in1(R1_q), .out(multiplexer_2_out), .sel(decoder_1_out0));
  Negator #(.width(32)) negator_1 (.in(out1), .out(negator_1_out));
  or or_2 (or_2_out, decoder_1_out0, decoder_1_out2, decoder_1_out3);
  Multiplexer #(.width(32)) multiplexer_3 (
    .in0(multiplexer_2_out), .in1(negator_1_out), .out(multiplexer_3_out), .sel(decoder_1_out3));
  Register #(.width(32)) R2 (.D(multiplexer_3_out), .en(or_2_out), .clk(clk), .Q(out1));  // open: clr
endmodule
