// Logisim project RegisterFile.circ as structural Verilog: 3 circuits, main circuit main
module main (
  input  [4:0] Read0,
  input  [4:0] Read1,
  input  [4:0] Write,
  input  [31:0] Data,
  input  WriteReg,
  input  clk,
  input  rst,
  output [31:0] RegOut1,
  output [31:0] RegOut2
);

  wire decoder_1_out0, decoder_1_out1, decoder_1_out2, decoder_1_out3, decoder_1_out4, decoder_1_out5,
       decoder_1_out6, decoder_1_out7, rst_t;
  wire [31:0] RegOut1_1, RegOut1_2, RegOut1_3, RegOut1_4, RegOut1_5, RegOut1_6, RegOut1_7, RegOut1_8,
       RegOut2_1, RegOut2_2, RegOut2_3, RegOut2_4, RegOut2_5, RegOut2_6, RegOut2_7, RegOut2_8;

  ResetHandler resethandler_1 (.rst_in(rst), .clk(clk), .rst(rst_t));
  Decoder #(.select(3)) decoder_1 (
    .out0(decoder_1_out0), .out1(decoder_1_out1), .out2(decoder_1_out2), .out3(decoder_1_out3),
    .out4(decoder_1_out4), .out5(decoder_1_out5), .out6(decoder_1_out6), .out7(decoder_1_out7),
    .sel(Write[4:2]), .en(WriteReg));
  SubRegisterFile SubRegister000 (
    .isFirstRow(1'b1), .Read0(Read0[1:0]), .Read1(Read1[1:0]), .Write(Write[1:0]), .Data(Data),
    .WriteReg(decoder_1_out0), .clk(clk), .rst(rst_t), .RegOut1(RegOut1_1), .RegOut2(RegOut2_1));
  SubRegisterFile SubRegister001 (
    .isFirstRow(1'b0), .Read0(Read0[1:0]), .Read1(Read1[1:0]), .Write(Write[1:0]), .Data(Data),
    .WriteReg(decoder_1_out1), .clk(clk), .rst(rst_t), .RegOut1(RegOut1_2), .RegOut2(RegOut2_2));
  SubRegisterFile SubRegister010 (
    .isFirstRow(1'b0), .Read0(Read0[1:0]), .Read1(Read1[1:0]), .Write(Write[1:0]), .Data(Data),
    .WriteReg(decoder_1_out2), .clk(clk), .rst(rst_t), .RegOut1(RegOut1_3), .RegOut2(RegOut2_3));
  SubRegisterFile SubRegister011 (
    .isFirstRow(1'b0), .Read0(Read0[1:0]), .Read1(Read1[1:0]), .Write(Write[1:0]), .Data(Data),
    .WriteReg(decoder_1_out3), .clk(clk), .rst(rst_t), .RegOut1(RegOut1_4), .RegOut2(RegOut2_4));
  SubRegisterFile SubRegister100 (
    .isFirstRow(1'b0), .Read0(Read0[1:0]), .Read1(Read1[1:0]), .Write(Write[1:0]), .Data(Data),
    .WriteReg(decoder_1_out4), .clk(clk), .rst(rst_t), .RegOut1(RegOut1_5), .RegOut2(RegOut2_5));
  SubRegisterFile SubRegister101 (
    .isFirstRow(1'b0), .Read0(Read0[1:0]), .Read1(Read1[1:0]), .Write(Write[1:0]), .Data(Data),
    .WriteReg(decoder_1_out5), .clk(clk), .rst(rst_t), .RegOut1(RegOut1_6), .RegOut2(RegOut2_6));
  SubRegisterFile SubRegister110 (
    .isFirstRow(1'b0), .Read0(Read0[1:0]), .Read1(Read1[1:0]), .Write(Write[1:0]), .Data(Data),
    .WriteReg(decoder_1_out6), .clk(clk), .rst(rst_t), .RegOut1(RegOut1_7), .RegOut2(RegOut2_7));
  SubRegisterFile SubRegister111 (
    .isFirstRow(1'b0), .Read0(Read0[1:0]), .Read1(Read1[1:0]), .Write(Write[1:0]), .Data(Data),
    .WriteReg(decoder_1_out7), .clk(clk), .rst(rst_t), .RegOut1(RegOut1_8), .RegOut2(RegOut2_8));
  Multiplexer #(.select(3), .width(32)) multiplexer_1 (
    .in0(RegOut1_1), .in1(RegOut1_2), .in2(RegOut1_3), .in3(RegOut1_4), .in4(RegOut1_5), .in5(RegOut1_6),
    .in6(RegOut1_7), .in7(RegOut1_8), .out(RegOut1), .sel(Read0[4:2]));
  Multiplexer #(.select(3), .width(32)) multiplexer_2 (
    .in0(RegOut2_1), .in1(RegOut2_2), .in2(RegOut2_3), .in3(RegOut2_4), .in4(RegOut2_5), .in5(RegOut2_6),
    .in6(RegOut2_7), .in7(RegOut2_8), .out(RegOut2), .sel(Read1[4:2]));

  // Other names for the same wires on the sheet: Read0_t[1:0] = Read0[1:0]; Read0Select[2:0] = Read0[4:2];
  //   Read1_t[1:0] = Read1[1:0]; Read1Select[2:0] = Read1[4:2]; Write_t[1:0] = Write[1:0];
  //   WriteSelect[2:0] = Write[4:2]
endmodule

module SubRegisterFile (
  input  isFirstRow,
  input  [1:0] Read0,
  input  [1:0] Read1,
  input  [1:0] Write,
  input  [31:0] Data,
  input  WriteReg,
  input  clk,
  input  rst,
  output [31:0] RegOut1,
  output [31:0] RegOut2
);

  wire decoder_1_out0, decoder_1_out1, decoder_1_out2, decoder_1_out3;
  wire [31:0] multiplexer_1_out, R00_q, R01_q, R10_q, R11_q;

  Decoder #(.select(2)) decoder_1 (
    .out0(decoder_1_out0), .out1(decoder_1_out1), .out2(decoder_1_out2), .out3(decoder_1_out3), .sel(Write),
    .en(WriteReg));
  Multiplexer #(.width(32)) multiplexer_1 (.in0(Data), .in1({32{1'b0}}), .out(multiplexer_1_out), .sel(isFirstRow));
  Register #(.width(32)) R00 (.D(multiplexer_1_out), .en(decoder_1_out0), .clk(clk), .Q(R00_q), .clr(rst));
  Register #(.width(32)) R01 (.D(Data), .en(decoder_1_out1), .clk(clk), .Q(R01_q), .clr(rst));
  Register #(.width(32)) R10 (.D(Data), .en(decoder_1_out2), .clk(clk), .Q(R10_q), .clr(rst));
  Register #(.width(32)) R11 (.D(Data), .en(decoder_1_out3), .clk(clk), .Q(R11_q), .clr(rst));
  Multiplexer #(.select(2), .width(32)) multiplexer_2 (
    .in0(R00_q), .in1(R01_q), .in2(R10_q), .in3(R11_q), .out(RegOut1), .sel(Read0));
  Multiplexer #(.select(2), .width(32)) multiplexer_3 (
    .in0(R00_q), .in1(R01_q), .in2(R10_q), .in3(R11_q), .out(RegOut2), .sel(Read1));
endmodule

module ResetHandler (
  input  rst_in,
  input  clk,
  output rst
);

  wire d_ff_1_q, d_ff_2_q;

  D_Flip_Flop d_ff_1 (.D(1'b1), .clk(clk), .Q(d_ff_1_q));  // open: Qn, preset, reset
  D_Flip_Flop d_ff_2 (.D(d_ff_1_q), .clk(clk), .Q(d_ff_2_q));  // open: Qn, preset, reset
  Multiplexer multiplexer_1 (.in0(1'b1), .in1(rst_in), .out(rst), .sel(d_ff_2_q));
endmodule
