// Logisim project MipsCPU.circ as structural Verilog: 4 circuits, main circuit main
module main (
  input  clk,
  input  rst,
  input  Jen,
  input  [31:0] Jin,
  output InstDone,
  output [31:0] Jout,
  output [31:0] R0,
  output [31:0] R1,
  output [31:0] R2,
  output [31:0] R3,
  output [31:0] R4,
  output [31:0] R5,
  output [31:0] R6,
  output [31:0] R7,
  output [31:0] R8,
  output [31:0] R9,
  output [31:0] R10,
  output [31:0] R11,
  output [31:0] R12,
  output [31:0] R13,
  output [31:0] R14,
  output [31:0] R15,
  output [31:0] R16,
  output [31:0] R17,
  output [31:0] R18,
  output [31:0] R19,
  output [31:0] R20,
  output [31:0] R21,
  output [31:0] R22,
  output [31:0] R23,
  output [31:0] R24,
  output [31:0] R25,
  output [31:0] R26,
  output [31:0] R27,
  output [31:0] R28,
  output [31:0] R29,
  output [31:0] R30,
  output [31:0] R31
);

  wire ALUSrc, and_1_out, and_2_out, Branch, Jal, MemWrite, not_1_out, not_2_out, RegDst, RegWrite,
       ShiftInst, ShiftSRC, ZeroSignal;
  wire [1:0] ALUOp, Jump, MemToReg;
  wire [3:0] alucontrolunit_1_aluselector;
  wire [4:0] multiplexer_1_out, multiplexer_3_out;
  wire [5:0] funct;
  wire [31:0] adder_2_out, alu_1_res_low, and_3_out, Bin, bit_extender_2_out, bit_extender_3_out,
       DataMemoryJin, mipsmemory_2_dout, multiplexer_2_out, multiplexer_4_out, multiplexer_5_out,
       multiplexer_7_out, MuxOut, PC, RegisterFile_WriteData, RegOut1, RegOut2, SignExt_Immediate, UpdatedPC;
  wire [31:6] Instruction;

  Register #(.width(32)) u_PC (.D(multiplexer_4_out), .clk(clk), .Q(PC), .clr(rst));  // open: en
  Adder #(.width(32)) adder_1 (.a(PC), .b(32'h1), .out(UpdatedPC));  // open: cin, cout
  ControlUnit controlunit_1 (
    .Opcode(Instruction[31:26]), .funct(funct), .RegDst(RegDst), .AluOp(ALUOp), .RegWrite(RegWrite),
    .MemToReg(MemToReg), .MemWrite(MemWrite), .ALUSrc(ALUSrc), .Jump(Jump), .Branch(Branch), .Jal(Jal),
    .shiftInst(ShiftInst), .shiftSRC(ShiftSRC));
  Adder #(.width(32)) adder_2 (.a(UpdatedPC), .b(SignExt_Immediate), .out(adder_2_out));  // open: cin, cout
  not not_1 (not_1_out, ZeroSignal);
  Multiplexer #(.width(5)) multiplexer_1 (
    .in0(Instruction[20:16]), .in1(Instruction[15:11]), .out(multiplexer_1_out), .sel(RegDst));
  Multiplexer #(.width(32)) multiplexer_2 (
    .in0(UpdatedPC), .in1(adder_2_out), .out(multiplexer_2_out), .sel(and_1_out));
  and and_1 (and_1_out, not_1_out, Branch);
  MipsMemory mipsmemory_1 (
    .Jen(Jen), .Wen(1'b0), .Jin(Jin), .Addr(PC[8:0]), .clk(clk), .Dout({Instruction, funct}),
    .Jout(DataMemoryJin));  // open: Din
  Multiplexer #(.width(5)) multiplexer_3 (.in0(multiplexer_1_out), .in1({5{1'b1}}), .out(multiplexer_3_out), .sel(Jal));
  Multiplexer #(.select(2), .width(32)) multiplexer_4 (
    .in0(multiplexer_2_out), .in1({PC[31:26], Instruction[25:6], funct}), .in2(RegOut1), .in3(RegOut1),
    .out(multiplexer_4_out), .sel(Jump));
  RegisterFile registerfile_1 (
    .Read0(Instruction[25:21]), .Read1(Instruction[20:16]), .Write(multiplexer_3_out),
    .Data(RegisterFile_WriteData), .WriteReg(RegWrite), .clk(clk), .rst(rst), .RegOut1(RegOut1),
    .RegOut2(RegOut2), .Reg0(R0), .Reg1(R1), .Reg2(R2), .Reg3(R3), .Reg4(R4), .Reg5(R5), .Reg6(R6),
    .Reg7(R7), .Reg8(R8), .Reg9(R9), .Reg10(R10), .Reg11(R11), .Reg12(R12), .Reg13(R13), .Reg14(R14),
    .Reg15(R15), .Reg16(R16), .Reg17(R17), .Reg18(R18), .Reg19(R19), .Reg20(R20), .Reg21(R21), .Reg22(R22),
    .Reg23(R23), .Reg24(R24), .Reg25(R25), .Reg26(R26), .Reg27(R27), .Reg28(R28), .Reg29(R29), .Reg30(R30),
    .Reg31(R31));
  assign SignExt_Immediate = {{16{Instruction[15]}}, {Instruction[15:6], funct}};  // Bit_Extender bit_extender_1
  not not_2 (not_2_out, ShiftSRC);
  and and_2 (and_2_out, ShiftInst, not_2_out);
  ALUControlUnit alucontrolunit_1 (.funct(funct), .ALUOp(ALUOp), .ALUSelector(alucontrolunit_1_aluselector));
  Multiplexer #(.width(32)) multiplexer_5 (.in0(RegOut1), .in1(RegOut2), .out(multiplexer_5_out), .sel(and_2_out));
  Multiplexer #(.width(32)) multiplexer_6 (.in0(SignExt_Immediate), .in1(RegOut2), .out(MuxOut), .sel(ALUSrc));
  assign bit_extender_2_out = {{27{1'b0}}, Instruction[10:6]};  // Bit_Extender bit_extender_2
  Multiplexer #(.width(32)) multiplexer_7 (
    .in0(bit_extender_2_out), .in1(RegOut2), .out(multiplexer_7_out), .sel(ShiftSRC));
  Multiplexer #(.width(32)) multiplexer_8 (.in0(MuxOut), .in1(multiplexer_7_out), .out(Bin), .sel(ShiftInst));
  ALU alu_1 (
    .a(multiplexer_5_out), .b(Bin), .aluop(alucontrolunit_1_aluselector), .output_inverted(1'b0),
    .output_inc(1'b0), .clk(clk), .rst(rst), .res_low(alu_1_res_low));  // open: res_high, done
  Comparator #(.width(32)) comparator_1 (.a({32{1'b0}}), .b(alu_1_res_low), .eq(ZeroSignal));  // open: gt, lt
  assign and_3_out = UpdatedPC & 32'h1ff;  // AND_Gate and_3, 32 bits wide
  MipsMemory mipsmemory_2 (
    .Jen(Jen), .Wen(MemWrite), .Din(RegOut2), .Jin(DataMemoryJin), .Addr(alu_1_res_low[8:0]), .clk(clk),
    .Dout(mipsmemory_2_dout), .Jout(Jout));
  assign bit_extender_3_out = {{31{1'b0}}, alu_1_res_low[31]};  // Bit_Extender bit_extender_3
  Multiplexer #(.select(2), .width(32)) multiplexer_9 (
    .in0(mipsmemory_2_dout), .in1(alu_1_res_low), .in2(and_3_out), .in3(bit_extender_3_out),
    .out(RegisterFile_WriteData), .sel(MemToReg));

  assign InstDone = 1'b1;

  // Other names for the same wires on the sheet: rt[4:0] = Instruction[20:16]; rs[4:0] = Instruction[25:21];
  //   Instruction[5:0] = funct; shamt[4:0] = Instruction[10:6]; rd[4:0] = Instruction[15:11];
  //   Opcode[5:0] = Instruction[31:26]
endmodule

module ALUControlUnit (
  input  [5:0] funct,
  input  [1:0] ALUOp,
  output [3:0] ALUSelector
);

  ROM #(.dataWidth(4)) rom_1 (.addr({ALUOp, funct}), .data(ALUSelector));

  // Notes on the sheet:
  //   contents of rom_1 (hex, n*v repeats v):
  //   64*0 64*1 9 0 0 0 9 0 a b 26*0 1 0 4 5 6
endmodule

module ALUDecoder (
  input  O5,
  input  O4,
  input  O3,
  input  O2,
  input  O1,
  input  O0,
  output ALUOP1,
  output ALUOP0
);

  wire and_2_out, and_3_out, not_1_out, not_2_out, not_3_out, not_4_out, not_5_out, not_6_out;

  not not_1 (not_1_out, O5);
  not not_2 (not_2_out, O4);
  not not_3 (not_3_out, O3);
  not not_4 (not_4_out, O2);
  not not_5 (not_5_out, O1);
  not not_6 (not_6_out, O0);
  and and_1 (ALUOP1, not_2_out, not_3_out, not_4_out, not_5_out, not_6_out);
  and and_2 (and_2_out, not_1_out, not_2_out, not_3_out, O2, not_5_out, O0);
  and and_3 (and_3_out, not_1_out, not_2_out, O3, not_4_out, O1, not_6_out);
  or or_1 (ALUOP0, and_2_out, and_3_out);
endmodule

module ControlUnit (
  input  [5:0] Opcode,
  input  [5:0] funct,
  output RegDst,
  output [1:0] AluOp,
  output RegWrite,
  output [1:0] MemToReg,
  output MemWrite,
  output ALUSrc,
  output [1:0] Jump,
  output Branch,
  output Jal,
  output shiftInst,
  output shiftSRC
);

  wire comparator_1_eq, comparator_2_eq, comparator_3_eq, comparator_4_eq, comparator_6_eq, comparator_7_eq,
       comparator_12_eq, comparator_13_eq, or_4_out;

  Comparator #(.width(6)) comparator_1 (.a(Opcode), .b(6'b100011), .eq(comparator_1_eq));  // open: gt, lt
  Comparator #(.width(6)) comparator_2 (.a(Opcode), .b({6{1'b0}}), .eq(comparator_2_eq));  // open: gt, lt
  Comparator #(.width(6)) comparator_3 (.a(Opcode), .b(6'b001000), .eq(comparator_3_eq));  // open: gt, lt
  Comparator #(.width(6)) comparator_4 (.a(Opcode), .b(6'b001010), .eq(comparator_4_eq));  // open: gt, lt
  or or_1 (RegWrite, comparator_1_eq, comparator_2_eq, comparator_4_eq, Jal, comparator_3_eq);
  Comparator #(.width(6)) comparator_5 (.a(Opcode), .b(6'b000011), .eq(Jal));  // open: gt, lt
  Comparator #(.width(6)) comparator_6 (.a(Opcode), .b(6'b000010), .eq(comparator_6_eq));  // open: gt, lt
  Comparator #(.width(6)) comparator_7 (.a(funct), .b(6'b001000), .eq(comparator_7_eq));  // open: gt, lt
  Comparator #(.width(6)) comparator_8 (.a(Opcode), .b(6'b000101), .eq(Branch));  // open: gt, lt
  Comparator #(.width(6)) comparator_9 (.a(Opcode), .b({6{1'b0}}), .eq(RegDst));  // open: gt, lt
  ALUDecoder ALUDecoder_1 (
    .O5(Opcode[5]), .O4(Opcode[4]), .O3(Opcode[3]), .O2(Opcode[2]), .O1(Opcode[1]), .O0(Opcode[0]),
    .ALUOP1(AluOp[1]), .ALUOP0(AluOp[0]));
  Comparator #(.width(6)) comparator_10 (.a(Opcode), .b(6'b101011), .eq(MemWrite));  // open: gt, lt
  or or_2 (Jump[0], Jal, comparator_6_eq);
  and and_1 (Jump[1], comparator_7_eq, comparator_2_eq);
  Comparator #(.width(6)) comparator_11 (.a(funct), .b(6'b000100), .eq(shiftSRC));  // open: gt, lt
  Comparator #(.width(6)) comparator_12 (.a(funct), .b({6{1'b0}}), .eq(comparator_12_eq));  // open: gt, lt
  Comparator #(.width(6)) comparator_13 (.a(Opcode), .b(6'b001000), .eq(comparator_13_eq));  // open: gt, lt
  or or_3 (ALUSrc, comparator_2_eq, Branch);
  or or_4 (or_4_out, shiftSRC, comparator_12_eq);
  or or_5 (MemToReg[0], comparator_2_eq, comparator_4_eq, comparator_13_eq);
  or or_6 (MemToReg[1], comparator_4_eq, Jal);
  and and_2 (shiftInst, or_4_out, comparator_2_eq);
endmodule
