// Logisim project MipsCPUMultiCycle.circ as structural Verilog: 4 circuits, main circuit main
module main (
  input  clk,
  input  rst,
  input  Jen,
  input  [31:0] Jin,
  output [31:0] Jout,
  output [31:0] R0,
  output [31:0] R1,
  output [31:0] R2,
  output [31:0] R3,
  output [31:0] R4,
  output [31:0] R5,
  output [31:0] R6,
  output [31:0] R7,
  output [31:0] R8,
  output [31:0] R9,
  output [31:0] R10,
  output [31:0] R11,
  output [31:0] R12,
  output [31:0] R13,
  output [31:0] R14,
  output [31:0] R15,
  output [31:0] R16,
  output [31:0] R17,
  output [31:0] R18,
  output [31:0] R19,
  output [31:0] R20,
  output [31:0] R21,
  output [31:0] R22,
  output [31:0] R23,
  output [31:0] R24,
  output [31:0] R25,
  output InstDone,
  output [31:0] R26,
  output [31:0] R27,
  output [31:0] R28,
  output [31:0] R29,
  output [31:0] R30,
  output [31:0] R31
);

  wire ALUPcController, ALUSrc, and_1_out, Branch, Controller2, IR_WE, Jal, MemWrite, not_1_out, not_3_out,
       not_4_out, not_5_out, or_1_out, PC_WE, PCSelect, RegDst, RegWrite, ShiftInst, ShiftSRC, ZeroSignal;
  wire [1:0] ALUOp, and_2_out, and_3_out, MemToReg, PCSource;
  wire [3:0] ALUControlUnit_1_aluselector, multiplexer_7_out;
  wire [4:0] multiplexer_2_out, multiplexer_3_out;
  wire [5:0] funct;
  wire [30:0] alu_1_res_low;
  wire [31:0] ALUout, ALUSrcB, and_5_out, bit_extender_2_out, bit_extender_3_out, DataMemoryJin,
       MemoryDataRegister_q, mipsmemory_1_dout, mipsmemory_2_dout, multiplexer_1_out, multiplexer_4_out,
       multiplexer_5_out, multiplexer_8_out, multiplexer_9_out, MuxOut, PC, registerfile_1_regout1,
       registerfile_1_regout2, RegisterFile_WriteData, RegOut1, RegOut2, SignExt_Immediate;
  wire [31:6] Instruction;
  wire [31:31] alu_1_res_low_2;

  Multiplexer #(.width(32)) multiplexer_1 (
    .in0(multiplexer_4_out), .in1({alu_1_res_low_2[31], alu_1_res_low}), .out(multiplexer_1_out),
    .sel(PCSelect));
  not not_1 (not_1_out, ZeroSignal);
  and and_1 (and_1_out, not_1_out, Branch);
  or or_1 (or_1_out, PC_WE, and_1_out);
  Register #(.width(32)) u_PC (.D(multiplexer_1_out), .en(or_1_out), .clk(clk), .Q(PC), .clr(rst));
  ControlUnit ControlUnit_1 (
    .Opcode(Instruction[31:26]), .funct(funct), .clk(clk), .rst(rst), .RegDst(RegDst), .RegWrite(RegWrite),
    .ALUop(ALUOp), .MemToReg(MemToReg), .MemWrite(MemWrite), .ALUSrc(ALUSrc), .PCSource(PCSource),
    .Branch(Branch), .Jal(Jal), .shiftInst(ShiftInst), .shiftSRC(ShiftSRC), .PCSelect(PCSelect),
    .PC_WE(PC_WE), .InstDone(InstDone), .IR_WE(IR_WE), .ALUPcController(ALUPcController),
    .Controller2(Controller2));
  Multiplexer #(.width(5)) multiplexer_2 (
    .in0(Instruction[20:16]), .in1(Instruction[15:11]), .out(multiplexer_2_out), .sel(RegDst));
  Multiplexer #(.width(5)) multiplexer_3 (.in0(multiplexer_2_out), .in1({5{1'b1}}), .out(multiplexer_3_out), .sel(Jal));
  MipsMemory mipsmemory_1 (
    .Jen(Jen), .Wen(1'b0), .Jin(Jin), .Addr(PC[8:0]), .clk(clk), .Dout(mipsmemory_1_dout),
    .Jout(DataMemoryJin));  // open: Din
  Register #(.width(32)) Instruction_Register (
    .D(mipsmemory_1_dout), .en(IR_WE), .clk(clk), .Q({Instruction, funct}), .clr(rst));
  Multiplexer #(.select(2), .width(32)) multiplexer_4 (
    .in0(ALUout), .in1({PC[31:26], Instruction[25:6], funct}), .in2(RegOut1), .in3(RegOut1),
    .out(multiplexer_4_out), .sel(PCSource));
  RegisterFile registerfile_1 (
    .Read0(Instruction[25:21]), .Read1(Instruction[20:16]), .Write(multiplexer_3_out),
    .Data(RegisterFile_WriteData), .WriteReg(RegWrite), .clk(clk), .rst(rst),
    .RegOut1(registerfile_1_regout1), .RegOut2(registerfile_1_regout2), .Reg0(R0), .Reg1(R1), .Reg2(R2),
    .Reg3(R3), .Reg4(R4), .Reg5(R5), .Reg6(R6), .Reg7(R7), .Reg8(R8), .Reg9(R9), .Reg10(R10), .Reg11(R11),
    .Reg12(R12), .Reg13(R13), .Reg14(R14), .Reg15(R15), .Reg16(R16), .Reg17(R17), .Reg18(R18), .Reg19(R19),
    .Reg20(R20), .Reg21(R21), .Reg22(R22), .Reg23(R23), .Reg24(R24), .Reg25(R25), .Reg26(R26), .Reg27(R27),
    .Reg28(R28), .Reg29(R29), .Reg30(R30), .Reg31(R31));
  assign SignExt_Immediate = {{16{Instruction[15]}}, {Instruction[15:6], funct}};  // Bit_Extender bit_extender_1
  Register #(.width(32)) ReadData2 (.D(registerfile_1_regout2), .clk(clk), .Q(RegOut2), .clr(rst));  // open: en
  not not_2 (and_2_out[1], ALUPcController);
  ALUControlUnit ALUControlUnit_1 (.funct(funct), .ALUOp(ALUOp), .ALUSelector(ALUControlUnit_1_aluselector));
  Multiplexer #(.select(2), .width(32)) multiplexer_5 (
    .in0(RegOut1), .in1(RegOut2), .in2(PC), .in3(PC), .out(multiplexer_5_out), .sel(and_2_out));
  Multiplexer #(.width(32)) multiplexer_6 (.in0(SignExt_Immediate), .in1(RegOut2), .out(MuxOut), .sel(ALUSrc));
  Multiplexer #(.width(4)) multiplexer_7 (
    .in0(4'b0000), .in1(ALUControlUnit_1_aluselector), .out(multiplexer_7_out), .sel(ALUPcController));
  Register #(.width(32)) ReadData1 (.D(registerfile_1_regout1), .clk(clk), .Q(RegOut1), .clr(rst));  // open: en
  assign bit_extender_2_out = {{27{1'b0}}, Instruction[10:6]};  // Bit_Extender bit_extender_2
  and and_2 (and_2_out[0], ShiftInst, not_3_out);
  Multiplexer #(.width(32)) multiplexer_8 (
    .in0(bit_extender_2_out), .in1(RegOut2), .out(multiplexer_8_out), .sel(ShiftSRC));
  not not_3 (not_3_out, ShiftSRC);
  Multiplexer #(.width(32)) multiplexer_9 (
    .in0(MuxOut), .in1(multiplexer_8_out), .out(multiplexer_9_out), .sel(ShiftInst));
  ALU alu_1 (
    .a(multiplexer_5_out), .b(ALUSrcB), .aluop(multiplexer_7_out), .output_inverted(1'b0), .output_inc(1'b0),
    .clk(clk), .rst(rst), .res_low({alu_1_res_low_2[31], alu_1_res_low}));  // open: res_high, done
  not not_4 (not_4_out, Controller2);
  not not_5 (not_5_out, ALUPcController);
  Register #(.width(32)) u_ALUOut (
    .D({alu_1_res_low_2[31], alu_1_res_low}), .clk(clk), .Q(ALUout), .clr(rst));  // open: en
  Comparator #(.width(32)) comparator_1 (
    .a({alu_1_res_low_2[31], alu_1_res_low}), .b({32{1'b0}}), .eq(ZeroSignal));  // open: gt, lt
  and and_3 (and_3_out[0], not_4_out, not_5_out);
  and and_4 (and_3_out[1], not_5_out, Controller2);
  Multiplexer #(.select(2), .width(32)) multiplexer_10 (
    .in0(multiplexer_9_out), .in1(32'h1), .in2(SignExt_Immediate), .out(ALUSrcB), .sel(and_3_out));  // open: in3
  assign and_5_out = PC & 32'h1ff;  // AND_Gate and_5, 32 bits wide
  MipsMemory mipsmemory_2 (
    .Jen(Jen), .Wen(MemWrite), .Din(RegOut2), .Jin(DataMemoryJin), .Addr(ALUout[8:0]), .clk(clk),
    .Dout(mipsmemory_2_dout), .Jout(Jout));
  Register #(.width(32)) MemoryDataRegister (
    .D(mipsmemory_2_dout), .clk(clk), .Q(MemoryDataRegister_q), .clr(rst));  // open: en
  assign bit_extender_3_out = {{31{1'b0}}, alu_1_res_low_2[31]};  // Bit_Extender bit_extender_3
  Multiplexer #(.select(2), .width(32)) multiplexer_11 (
    .in0(MemoryDataRegister_q), .in1(ALUout), .in2(and_5_out), .in3(bit_extender_3_out),
    .out(RegisterFile_WriteData), .sel(MemToReg));

  // Other names for the same wires on the sheet: Instruction[5:0] = funct; shamt[4:0] = Instruction[10:6];
  //   rd[4:0] = Instruction[15:11]; ALUoutRegister[31:0] = ALUout; rt[4:0] = Instruction[20:16];
  //   rs[4:0] = Instruction[25:21]; Opcode[5:0] = Instruction[31:26]
endmodule

module ALUControlUnit (
  input  [5:0] funct,
  input  [1:0] ALUOp,
  output [3:0] ALUSelector
);

  ROM #(.dataWidth(4)) HelperROM (.addr({ALUOp, funct}), .data(ALUSelector));

  // Notes on the sheet:
  //   contents of HelperROM (hex, n*v repeats v):
  //   64*0 64*1 9 0 0 0 9 0 a b 26*0 1 0 4 5 6
endmodule

module ALUDecoder (
  input  O5,
  input  O4,
  input  O3,
  input  O2,
  input  O1,
  input  O0,
  output ALUOP1,
  output ALUOP0
);

  wire and_2_out, and_3_out, not_1_out, not_2_out, not_3_out, not_4_out, not_5_out, not_6_out;

  not not_1 (not_1_out, O5);
  not not_2 (not_2_out, O4);
  not not_3 (not_3_out, O3);
  not not_4 (not_4_out, O2);
  not not_5 (not_5_out, O1);
  not not_6 (not_6_out, O0);
  and and_1 (ALUOP1, not_2_out, not_3_out, not_4_out, not_5_out, not_6_out);
  and and_2 (and_2_out, not_1_out, not_2_out, not_3_out, O2, not_5_out, O0);
  and and_3 (and_3_out, not_1_out, not_2_out, O3, not_4_out, O1, not_6_out);
  or or_1 (ALUOP0, and_2_out, and_3_out);
endmodule

module ControlUnit (
  input  [5:0] Opcode,
  input  [5:0] funct,
  input  clk,
  input  rst,
  output RegDst,
  output RegWrite,
  output [1:0] ALUop,
  output [1:0] MemToReg,
  output MemWrite,
  output ALUSrc,
  output [1:0] PCSource,
  output Branch,
  output Jal,
  output shiftInst,
  output shiftSRC,
  output PCSelect,
  output PC_WE,
  output InstDone,
  output IR_WE,
  output ALUPcController,
  output Controller2
);

  wire and_3_out, comparator_1_eq, comparator_2_eq, comparator_3_eq, comparator_4_eq, comparator_5_eq,
       comparator_6_eq, comparator_7_eq, comparator_10_eq, comparator_11_eq, comparator_15_eq,
       comparator_17_eq, comparator_18_eq, comparator_20_eq, comparator_21_eq, or_4_out;
  wire [3:0] State, StateROM_data;

  Comparator #(.width(4)) comparator_1 (.a(State), .b(4'b0100), .eq(comparator_1_eq));  // open: gt, lt
  Comparator #(.width(4)) comparator_2 (.a(State), .b(4'b0111), .eq(comparator_2_eq));  // open: gt, lt
  Comparator #(.width(4)) comparator_3 (.a(State), .b(4'b1001), .eq(comparator_3_eq));  // open: gt, lt
  Comparator #(.width(4)) comparator_4 (.a(State), .b(4'b1010), .eq(comparator_4_eq));  // open: gt, lt
  Comparator #(.width(4)) comparator_5 (.a(State), .b(4'b1100), .eq(comparator_5_eq));  // open: gt, lt
  Register #(.width(4)) StateRegisters (.D(StateROM_data), .clk(clk), .Q(State), .clr(rst));  // open: en
  or or_1 (RegWrite, comparator_1_eq, comparator_2_eq, comparator_5_eq, comparator_3_eq, comparator_4_eq);
  ROM #(.addrWidth(10), .dataWidth(4)) StateROM (.addr({State, Opcode}), .data(StateROM_data));
  Comparator #(.width(6)) comparator_6 (.a(Opcode), .b({6{1'b0}}), .eq(comparator_6_eq));  // open: gt, lt
  Comparator #(.width(6)) comparator_7 (.a(Opcode), .b(6'b001010), .eq(comparator_7_eq));  // open: gt, lt
  Comparator #(.width(4)) comparator_8 (.a(State), .b(4'b0101), .eq(MemWrite));  // open: gt, lt
  Comparator #(.width(6)) comparator_9 (.a(Opcode), .b(6'b000011), .eq(Jal));  // open: gt, lt
  Comparator #(.width(6)) comparator_10 (.a(Opcode), .b(6'b000010), .eq(comparator_10_eq));  // open: gt, lt
  Comparator #(.width(6)) comparator_11 (.a(funct), .b(6'b001000), .eq(comparator_11_eq));  // open: gt, lt
  Comparator #(.width(6)) comparator_12 (.a(Opcode), .b(6'b000101), .eq(Branch));  // open: gt, lt
  Comparator #(.width(6)) comparator_13 (.a(Opcode), .b({6{1'b0}}), .eq(RegDst));  // open: gt, lt
  or or_2 (PCSource[0], Jal, comparator_10_eq);
  and and_1 (PCSource[1], comparator_11_eq, comparator_6_eq);
  Comparator #(.width(6)) comparator_14 (.a(funct), .b(6'b000100), .eq(shiftSRC));  // open: gt, lt
  Comparator #(.width(6)) comparator_15 (.a(funct), .b({6{1'b0}}), .eq(comparator_15_eq));  // open: gt, lt
  Comparator #(.width(4)) comparator_16 (.a(State), .b(4'b0000), .eq(InstDone));  // open: gt, lt
  Comparator #(.width(4)) comparator_17 (.a(State), .b(4'b1001), .eq(comparator_17_eq));  // open: gt, lt
  Comparator #(.width(4)) comparator_18 (.a(State), .b(4'b0111), .eq(comparator_18_eq));  // open: gt, lt
  Comparator #(.width(4)) comparator_19 (.a(State), .b(4'b0001), .eq(Controller2));  // open: gt, lt
  ALUDecoder ALUDecoder_1 (
    .O5(Opcode[5]), .O4(Opcode[4]), .O3(Opcode[3]), .O2(Opcode[2]), .O1(Opcode[1]), .O0(Opcode[0]),
    .ALUOP1(ALUop[1]), .ALUOP0(ALUop[0]));
  Comparator #(.width(6)) comparator_20 (.a(Opcode), .b(6'b001000), .eq(comparator_20_eq));  // open: gt, lt
  or or_3 (ALUSrc, comparator_6_eq, Branch);
  or or_4 (or_4_out, shiftSRC, comparator_15_eq);
  Comparator #(.width(4)) comparator_21 (.a(State), .b(4'b0000), .eq(comparator_21_eq));  // open: gt, lt
  or or_5 (MemToReg[0], comparator_6_eq, comparator_7_eq, comparator_20_eq);
  or or_6 (MemToReg[1], comparator_7_eq, Jal);
  and and_2 (shiftInst, or_4_out, comparator_6_eq);
  and and_3 (and_3_out, PCSource[1], comparator_18_eq);
  nor nor_1 (ALUPcController, comparator_21_eq, Controller2);
  or or_7 (PC_WE, and_3_out, InstDone, comparator_17_eq);

  assign IR_WE = InstDone;
  assign PCSelect = InstDone;

  // Other names for the same wires on the sheet: jr = PCSource[1]; RegWriteCondition = RegWrite

  // Notes on the sheet:
  //   contents of StateROM (hex, n*v repeats v):
  //   64*1 6 0 9 9 0 8 0 0 6 0 a 24*0 2 7*0 2 55*0 3 7*0 5 20*0 64*4 128*0 8*7 b 55*7 264*0 c
endmodule
