// Logisim project MipsMemory.circ as structural Verilog: 3 circuits, main circuit MipsMemory
module MipsMemory (
  input  Jen,
  input  Wen,
  input  [31:0] Din,
  input  [31:0] Jin,
  input  [8:0] Addr,
  input  clk,
  output [31:0] Dout,
  output [31:0] Jout
);

  wire decoder_1_out0, decoder_1_out1, decoder_1_out2, decoder_1_out3, decoder_1_out4, decoder_1_out5,
       decoder_1_out6, decoder_1_out7;
  wire [31:0] Dout1, Dout2, Dout3, Dout4, Dout5, Dout6, Dout7, Dout8, submemorylevel1_1_jout,
       submemorylevel1_2_jout, submemorylevel1_3_jout, submemorylevel1_4_jout, submemorylevel1_5_jout,
       submemorylevel1_6_jout, submemorylevel1_7_jout;

  Decoder #(.select(3)) decoder_1 (
    .out0(decoder_1_out0), .out1(decoder_1_out1), .out2(decoder_1_out2), .out3(decoder_1_out3),
    .out4(decoder_1_out4), .out5(decoder_1_out5), .out6(decoder_1_out6), .out7(decoder_1_out7),
    .sel(Addr[8:6]), .en(Wen));
  SubMemoryLevel1 submemorylevel1_1 (
    .Jen(Jen), .Wen(decoder_1_out0), .Din(Din), .Jin(Jin), .Addr(Addr[5:0]), .clk(clk), .Dout(Dout1),
    .Jout(submemorylevel1_1_jout));
  SubMemoryLevel1 submemorylevel1_2 (
    .Jen(Jen), .Wen(decoder_1_out1), .Din(Din), .Jin(submemorylevel1_1_jout), .Addr(Addr[5:0]), .clk(clk),
    .Dout(Dout2), .Jout(submemorylevel1_2_jout));
  SubMemoryLevel1 submemorylevel1_3 (
    .Jen(Jen), .Wen(decoder_1_out2), .Din(Din), .Jin(submemorylevel1_2_jout), .Addr(Addr[5:0]), .clk(clk),
    .Dout(Dout3), .Jout(submemorylevel1_3_jout));
  SubMemoryLevel1 submemorylevel1_4 (
    .Jen(Jen), .Wen(decoder_1_out3), .Din(Din), .Jin(submemorylevel1_3_jout), .Addr(Addr[5:0]), .clk(clk),
    .Dout(Dout4), .Jout(submemorylevel1_4_jout));
  SubMemoryLevel1 submemorylevel1_5 (
    .Jen(Jen), .Wen(decoder_1_out4), .Din(Din), .Jin(submemorylevel1_4_jout), .Addr(Addr[5:0]), .clk(clk),
    .Dout(Dout5), .Jout(submemorylevel1_5_jout));
  SubMemoryLevel1 submemorylevel1_6 (
    .Jen(Jen), .Wen(decoder_1_out5), .Din(Din), .Jin(submemorylevel1_5_jout), .Addr(Addr[5:0]), .clk(clk),
    .Dout(Dout6), .Jout(submemorylevel1_6_jout));
  SubMemoryLevel1 submemorylevel1_7 (
    .Jen(Jen), .Wen(decoder_1_out6), .Din(Din), .Jin(submemorylevel1_6_jout), .Addr(Addr[5:0]), .clk(clk),
    .Dout(Dout7), .Jout(submemorylevel1_7_jout));
  SubMemoryLevel1 submemorylevel1_8 (
    .Jen(Jen), .Wen(decoder_1_out7), .Din(Din), .Jin(submemorylevel1_7_jout), .Addr(Addr[5:0]), .clk(clk),
    .Dout(Dout8), .Jout(Jout));
  Multiplexer #(.select(3), .width(32)) multiplexer_1 (
    .in0(Dout1), .in1(Dout2), .in2(Dout3), .in3(Dout4), .in4(Dout5), .in5(Dout6), .in6(Dout7), .in7(Dout8),
    .out(Dout), .sel(Addr[8:6]));

  // Other names for the same wires on the sheet: Addr_t[5:0] = Addr[5:0]; AddrSelect[2:0] = Addr[8:6]
endmodule

module SubMemoryLevel1 (
  input  Jen,
  input  Wen,
  input  [31:0] Din,
  input  [31:0] Jin,
  input  [5:0] Addr,
  input  clk,
  output [31:0] Dout,
  output [31:0] Jout
);

  wire decoder_1_out0, decoder_1_out1, decoder_1_out2, decoder_1_out3, decoder_1_out4, decoder_1_out5,
       decoder_1_out6, decoder_1_out7;
  wire [31:0] Dout1, Dout2, Dout3, Dout4, Dout5, Dout6, Dout7, Dout8, submemorylevel2_1_jout,
       submemorylevel2_2_jout, submemorylevel2_3_jout, submemorylevel2_4_jout, submemorylevel2_5_jout,
       submemorylevel2_6_jout, submemorylevel2_7_jout;

  Decoder #(.select(3)) decoder_1 (
    .out0(decoder_1_out0), .out1(decoder_1_out1), .out2(decoder_1_out2), .out3(decoder_1_out3),
    .out4(decoder_1_out4), .out5(decoder_1_out5), .out6(decoder_1_out6), .out7(decoder_1_out7),
    .sel(Addr[5:3]), .en(Wen));
  SubMemoryLevel2 submemorylevel2_1 (
    .Jen(Jen), .Wen(decoder_1_out0), .Din(Din), .Jin(Jin), .Addr(Addr[2:0]), .clk(clk), .Dout(Dout1),
    .Jout(submemorylevel2_1_jout));
  SubMemoryLevel2 submemorylevel2_2 (
    .Jen(Jen), .Wen(decoder_1_out1), .Din(Din), .Jin(submemorylevel2_1_jout), .Addr(Addr[2:0]), .clk(clk),
    .Dout(Dout2), .Jout(submemorylevel2_2_jout));
  SubMemoryLevel2 submemorylevel2_3 (
    .Jen(Jen), .Wen(decoder_1_out2), .Din(Din), .Jin(submemorylevel2_2_jout), .Addr(Addr[2:0]), .clk(clk),
    .Dout(Dout3), .Jout(submemorylevel2_3_jout));
  SubMemoryLevel2 submemorylevel2_4 (
    .Jen(Jen), .Wen(decoder_1_out3), .Din(Din), .Jin(submemorylevel2_3_jout), .Addr(Addr[2:0]), .clk(clk),
    .Dout(Dout4), .Jout(submemorylevel2_4_jout));
  SubMemoryLevel2 submemorylevel2_5 (
    .Jen(Jen), .Wen(decoder_1_out4), .Din(Din), .Jin(submemorylevel2_4_jout), .Addr(Addr[2:0]), .clk(clk),
    .Dout(Dout5), .Jout(submemorylevel2_5_jout));
  SubMemoryLevel2 submemorylevel2_6 (
    .Jen(Jen), .Wen(decoder_1_out5), .Din(Din), .Jin(submemorylevel2_5_jout), .Addr(Addr[2:0]), .clk(clk),
    .Dout(Dout6), .Jout(submemorylevel2_6_jout));
  SubMemoryLevel2 submemorylevel2_7 (
    .Jen(Jen), .Wen(decoder_1_out6), .Din(Din), .Jin(submemorylevel2_6_jout), .Addr(Addr[2:0]), .clk(clk),
    .Dout(Dout7), .Jout(submemorylevel2_7_jout));
  SubMemoryLevel2 submemorylevel2_8 (
    .Jen(Jen), .Wen(decoder_1_out7), .Din(Din), .Jin(submemorylevel2_7_jout), .Addr(Addr[2:0]), .clk(clk),
    .Dout(Dout8), .Jout(Jout));
  Multiplexer #(.select(3), .width(32)) multiplexer_1 (
    .in0(Dout1), .in1(Dout2), .in2(Dout3), .in3(Dout4), .in4(Dout5), .in5(Dout6), .in6(Dout7), .in7(Dout8),
    .out(Dout), .sel(Addr[5:3]));

  // Other names for the same wires on the sheet: Addr_t[2:0] = Addr[2:0]; AddrSelect[2:0] = Addr[5:3]
endmodule

module SubMemoryLevel2 (
  input  Jen,
  input  Wen,
  input  [31:0] Din,
  input  [31:0] Jin,
  input  [2:0] Addr,
  input  clk,
  output [31:0] Dout,
  output [31:0] Jout
);

  wire Decoder000, Decoder001, Decoder010, Decoder011, Decoder100, Decoder101, Decoder110, Decoder111,
       or_1_out, or_2_out, or_3_out, or_4_out, or_5_out, or_6_out, or_7_out, or_8_out;
  wire [31:0] multiplexer_1_out, multiplexer_2_out, multiplexer_3_out, multiplexer_4_out, multiplexer_5_out,
       multiplexer_6_out, multiplexer_7_out, multiplexer_8_out, R00_q, R01_q, R10_q, R11_q, register_1_q,
       register_2_q, register_3_q;

  Decoder #(.select(3)) decoder_1 (
    .out0(Decoder000), .out1(Decoder001), .out2(Decoder010), .out3(Decoder011), .out4(Decoder100),
    .out5(Decoder101), .out6(Decoder110), .out7(Decoder111), .sel(Addr), .en(Wen));
  Multiplexer #(.width(32)) multiplexer_1 (.in0(Din), .in1(Jin), .out(multiplexer_1_out), .sel(Jen));
  Multiplexer #(.width(32)) multiplexer_2 (.in0(Din), .in1(R00_q), .out(multiplexer_2_out), .sel(Jen));
  Multiplexer #(.width(32)) multiplexer_3 (.in0(Din), .in1(R01_q), .out(multiplexer_3_out), .sel(Jen));
  Multiplexer #(.width(32)) multiplexer_4 (.in0(Din), .in1(R10_q), .out(multiplexer_4_out), .sel(Jen));
  or or_1 (or_1_out, Jen, Decoder000);
  or or_2 (or_2_out, Jen, Decoder001);
  or or_3 (or_3_out, Jen, Decoder010);
  or or_4 (or_4_out, Jen, Decoder011);
  Register #(.width(32)) R00 (.D(multiplexer_1_out), .en(or_1_out), .clk(clk), .Q(R00_q));  // open: clr
  Register #(.width(32)) R01 (.D(multiplexer_2_out), .en(or_2_out), .clk(clk), .Q(R01_q));  // open: clr
  Register #(.width(32)) R10 (.D(multiplexer_3_out), .en(or_3_out), .clk(clk), .Q(R10_q));  // open: clr
  Register #(.width(32)) R11 (.D(multiplexer_4_out), .en(or_4_out), .clk(clk), .Q(R11_q));  // open: clr
  Multiplexer #(.width(32)) multiplexer_5 (.in0(Din), .in1(R11_q), .out(multiplexer_5_out), .sel(Jen));
  Multiplexer #(.width(32)) multiplexer_6 (.in0(Din), .in1(register_1_q), .out(multiplexer_6_out), .sel(Jen));
  Multiplexer #(.width(32)) multiplexer_7 (.in0(Din), .in1(register_2_q), .out(multiplexer_7_out), .sel(Jen));
  Multiplexer #(.width(32)) multiplexer_8 (.in0(Din), .in1(register_3_q), .out(multiplexer_8_out), .sel(Jen));
  or or_5 (or_5_out, Jen, Decoder100);
  or or_6 (or_6_out, Jen, Decoder101);
  or or_7 (or_7_out, Jen, Decoder110);
  or or_8 (or_8_out, Jen, Decoder111);
  Register #(.width(32)) register_1 (.D(multiplexer_5_out), .en(or_5_out), .clk(clk), .Q(register_1_q));  // open: clr
  Register #(.width(32)) register_2 (.D(multiplexer_6_out), .en(or_6_out), .clk(clk), .Q(register_2_q));  // open: clr
  Register #(.width(32)) register_3 (.D(multiplexer_7_out), .en(or_7_out), .clk(clk), .Q(register_3_q));  // open: clr
  Register #(.width(32)) register_4 (.D(multiplexer_8_out), .en(or_8_out), .clk(clk), .Q(Jout));  // open: clr
  Multiplexer #(.select(3), .width(32)) multiplexer_9 (
    .in0(R00_q), .in1(R01_q), .in2(R10_q), .in3(R11_q), .in4(register_1_q), .in5(register_2_q),
    .in6(register_3_q), .in7(Jout), .out(Dout), .sel(Addr));
endmodule
