// Logisim project MipsCPUPipeLined.circ as structural Verilog: 6 circuits, main circuit main
module main (
  input  clk,
  input  rst,
  input  Jen,
  input  [31:0] Jin,
  output [31:0] temp,
  output [31:0] Jout,
  output InstDone,
  output [31:0] R0,
  output [31:0] R1,
  output [31:0] R2,
  output [31:0] R3,
  output [31:0] R4,
  output [31:0] R5,
  output [31:0] R6,
  output [31:0] R7,
  output [31:0] R8,
  output [31:0] R9,
  output [31:0] R10,
  output [31:0] R11,
  output [31:0] R12,
  output [31:0] R13,
  output [31:0] R14,
  output [31:0] R15,
  output [31:0] R16,
  output [31:0] R17,
  output [31:0] R18,
  output [31:0] R19,
  output [31:0] R20,
  output [31:0] R21,
  output [31:0] R22,
  output [31:0] R23,
  output [31:0] R24,
  output [31:0] R25,
  output [31:0] R26,
  output [31:0] R27,
  output [31:0] R28,
  output [31:0] R29,
  output [31:0] R30,
  output [31:0] R31
);

  wire ALUSrc, and_1_out, and_2_out, and_3_out, and_5_out, Branch, comparator_1_eq, done, Jal, MemWrite,
       not_1_out, not_2_out, not_3_out, not_4_out, not_5_out, not_6_out, not_7_out, not_8_out, RegDst,
       RegWrite, ShiftInst, ShiftSRC, Stall, Stall2, Stall3, StallControl, ZeroSignal;
  wire [1:0] ALUOp, MemToReg, mfhi_mflo, PCSource;
  wire [3:0] ALUControlUnit_1_aluselector;
  wire [4:0] multiplexer_1_out, multiplexer_3_out, rd4, rs, rt4, rtRead, shamt;
  wire [5:0] funct, funct2, funct3, funct4, Opcode, Opcode2, Opcode3, Opcode4;
  wire [25:0] InstructionRegsiter1_jumpaddress;
  wire [31:0] adder_1_out, adder_2_out, alu_1_res_high, alu_1_res_low, ALUOut_q, ALUSrcB, and_6_out,
       bit_extender_1_out, bit_extender_2_out, BranchImmediate, DataMemoryJin, Hi,
       InstructionRegister3_instructionout, InstructionRegsiter1_instructionout, Lo, mipsmemory_1_dout,
       mipsmemory_2_dout, multiplexer_2_out, multiplexer_4_out, multiplexer_5_out, multiplexer_7_out,
       multiplexer_9_out, multiplexer_10_out, MuxOut, PC, register_1_q, RegisterFile_WriteData, RegOut1,
       RegOut1Branch, RegOut2, RegOut2Branch, SignExt_Immediate;

  Register #(.width(32)) u_PC (.D(multiplexer_4_out), .en(not_1_out), .clk(clk), .Q(PC), .clr(rst));
  not not_1 (not_1_out, Stall);
  ControlUnit ControlUnit_1 (
    .Opcode(Opcode), .funct(funct), .Opcode2(Opcode2), .funct2(funct2), .Opcode3(Opcode3), .funct3(funct3),
    .Opcode4(Opcode4), .funct4(funct4), .clk(clk), .rst(rst), .Stall(Stall), .RegDst(RegDst), .ALUop(ALUOp),
    .RegWrite(RegWrite), .MemToReg(MemToReg), .MemWrite(MemWrite), .ALUSrc(ALUSrc), .PCSource(PCSource),
    .Branch(Branch), .Jal(Jal), .shiftInst(ShiftInst), .shiftSRC(ShiftSRC), .StallControl(StallControl),
    .mfhi_mflo(mfhi_mflo), .Stall2(Stall2), .Stall3(Stall3));
  Register #(.width(32)) register_1 (.D(adder_1_out), .clk(clk), .Q(register_1_q), .clr(rst));  // open: en
  Adder #(.width(32)) adder_1 (.a(PC), .b(32'h1), .out(adder_1_out));  // open: cin, cout
  MipsMemory mipsmemory_1 (
    .Jen(Jen), .Wen(1'b0), .Jin(Jin), .Addr(PC[8:0]), .clk(clk), .Dout(mipsmemory_1_dout),
    .Jout(DataMemoryJin));  // open: Din
  Comparator #(.width(32)) comparator_1 (.a(RegOut1Branch), .b(RegOut2Branch), .eq(comparator_1_eq));  // open: gt, lt
  and and_1 (and_1_out, not_2_out, Branch);
  Adder #(.width(32)) adder_2 (.a(register_1_q), .b(BranchImmediate), .out(adder_2_out));  // open: cin, cout
  not not_2 (not_2_out, comparator_1_eq);
  Multiplexer #(.width(5)) multiplexer_1 (.in0(rt4), .in1(rd4), .out(multiplexer_1_out), .sel(RegDst));
  Multiplexer #(.width(32)) multiplexer_2 (
    .in0(adder_1_out), .in1(adder_2_out), .out(multiplexer_2_out), .sel(and_1_out));
  Multiplexer #(.width(5)) multiplexer_3 (.in0(multiplexer_1_out), .in1({5{1'b1}}), .out(multiplexer_3_out), .sel(Jal));
  IR_and_ID InstructionRegsiter1 (
    .Instruction(mipsmemory_1_dout), .Stall(Stall), .clk(clk), .rst(rst),
    .InstructionOut(InstructionRegsiter1_instructionout), .JumpAddress(InstructionRegsiter1_jumpaddress),
    .funct(funct), .shamt(shamt), .rt(rtRead), .rs(rs), .opcode(Opcode), .SignExt_Imd(BranchImmediate));  // open: rd
  and and_2 (and_2_out, not_3_out, RegWrite);
  not not_3 (not_3_out, Stall3);
  Multiplexer #(.select(2), .width(32)) multiplexer_4 (
    .in0(multiplexer_2_out), .in1({PC[31:26], InstructionRegsiter1_jumpaddress}), .in2(RegOut1Branch),
    .in3(RegOut1Branch), .out(multiplexer_4_out), .sel(PCSource));
  IR_and_ID InstructionRegsiter2 (
    .Instruction(InstructionRegsiter1_instructionout), .Stall(Stall), .clk(clk), .rst(rst),
    .InstructionOut(temp), .funct(funct2), .opcode(Opcode2), .SignExt_Imd(SignExt_Immediate));  // open: JumpAddress, shamt, rd, rt, rs
  RegisterFile registerfile_1 (
    .Read0(rs), .Read1(rtRead), .Write(multiplexer_3_out), .Data(RegisterFile_WriteData),
    .WriteReg(and_2_out), .clk(clk), .rst(rst), .RegOut1(RegOut1Branch), .RegOut2(RegOut2Branch), .Reg0(R0),
    .Reg1(R1), .Reg2(R2), .Reg3(R3), .Reg4(R4), .Reg5(R5), .Reg6(R6), .Reg7(R7), .Reg8(R8), .Reg9(R9),
    .Reg10(R10), .Reg11(R11), .Reg12(R12), .Reg13(R13), .Reg14(R14), .Reg15(R15), .Reg16(R16), .Reg17(R17),
    .Reg18(R18), .Reg19(R19), .Reg20(R20), .Reg21(R21), .Reg22(R22), .Reg23(R23), .Reg24(R24), .Reg25(R25),
    .Reg26(R26), .Reg27(R27), .Reg28(R28), .Reg29(R29), .Reg30(R30), .Reg31(R31));
  Register #(.width(32)) ReadData2 (.D(RegOut2Branch), .en(not_4_out), .clk(clk), .Q(RegOut2), .clr(rst));
  not not_4 (not_4_out, Stall);
  Register #(.width(32)) ReadData1 (.D(RegOut1Branch), .en(not_5_out), .clk(clk), .Q(RegOut1), .clr(rst));
  not not_5 (not_5_out, Stall);
  assign bit_extender_1_out = {{27{1'b0}}, shamt};  // Bit_Extender bit_extender_1
  Multiplexer #(.width(32)) multiplexer_5 (.in0(RegOut1), .in1(RegOut2), .out(multiplexer_5_out), .sel(and_3_out));
  Multiplexer #(.width(32)) multiplexer_6 (.in0(SignExt_Immediate), .in1(RegOut2), .out(MuxOut), .sel(ALUSrc));
  ALUControlUnit ALUControlUnit_1 (.funct(funct2), .ALUOp(ALUOp), .ALUSelector(ALUControlUnit_1_aluselector));
  Multiplexer #(.width(32)) multiplexer_7 (
    .in0(bit_extender_1_out), .in1(RegOut2), .out(multiplexer_7_out), .sel(ShiftSRC));
  and and_3 (and_3_out, ShiftInst, not_6_out);
  Multiplexer #(.width(32)) multiplexer_8 (.in0(MuxOut), .in1(multiplexer_7_out), .out(ALUSrcB), .sel(ShiftInst));
  not not_6 (not_6_out, ShiftSRC);
  ALU alu_1 (
    .a(multiplexer_5_out), .b(ALUSrcB), .aluop(ALUControlUnit_1_aluselector), .output_inverted(1'b0),
    .output_inc(1'b0), .clk(clk), .rst(rst), .res_low(alu_1_res_low), .res_high(alu_1_res_high), .done(done));
  not not_7 (not_7_out, done);
  and and_4 (Stall, StallControl, not_7_out);
  Register #(.width(32)) u_Lo (.D(alu_1_res_low), .en(StallControl), .clk(clk), .Q(Lo), .clr(rst));
  Register #(.width(32)) ALUOut (.D(alu_1_res_low), .clk(clk), .Q(ALUOut_q), .clr(rst));  // open: en
  Register #(.width(32)) u_Hi (.D(alu_1_res_high), .en(StallControl), .clk(clk), .Q(Hi), .clr(rst));
  IR_and_ID InstructionRegister3 (
    .Instruction(temp), .Stall(Stall2), .clk(clk), .rst(rst),
    .InstructionOut(InstructionRegister3_instructionout), .funct(funct3), .opcode(Opcode3));  // open: JumpAddress, shamt, rd, rt, rs, SignExt_Imd
  Comparator #(.width(32)) comparator_2 (.a(alu_1_res_low), .b({32{1'b0}}), .eq(ZeroSignal));  // open: gt, lt
  and and_5 (and_5_out, MemWrite, not_8_out);
  not not_8 (not_8_out, Stall2);
  MipsMemory mipsmemory_2 (
    .Jen(Jen), .Wen(and_5_out), .Din(RegOut2), .Jin(DataMemoryJin), .Addr(ALUOut_q[8:0]), .clk(clk),
    .Dout(mipsmemory_2_dout), .Jout(Jout));
  assign bit_extender_2_out = {{31{1'b0}}, ALUOut_q[31]};  // Bit_Extender bit_extender_2
  assign and_6_out = PC & 32'h1ff;  // AND_Gate and_6, 32 bits wide
  Multiplexer #(.select(2), .width(32)) multiplexer_9 (
    .in0(mipsmemory_2_dout), .in1(ALUOut_q), .in2(and_6_out), .in3(bit_extender_2_out),
    .out(multiplexer_9_out), .sel(MemToReg));
  IR_and_ID InstructionRegsiter4 (
    .Instruction(InstructionRegister3_instructionout), .Stall(Stall3), .clk(clk), .rst(rst), .funct(funct4),
    .rd(rd4), .rt(rt4), .opcode(Opcode4));  // open: InstructionOut, JumpAddress, shamt, rs, SignExt_Imd
  Register #(.width(32)) register_2 (
    .D(multiplexer_10_out), .clk(clk), .Q(RegisterFile_WriteData), .clr(rst));  // open: en
  Multiplexer #(.select(2), .width(32)) multiplexer_10 (
    .in0(multiplexer_9_out), .in1(Lo), .in2(Hi), .in3(Hi), .out(multiplexer_10_out), .sel(mfhi_mflo));
  InstDoneCircuit instdonecircuit_1 (.Stall3(Stall3), .clk(clk), .rst(rst), .InstDone(InstDone));

  // Other names for the same wires on the sheet: InstructionOut2[31:0] = temp
endmodule

module ALUControlUnit (
  input  [5:0] funct,
  input  [1:0] ALUOp,
  output [3:0] ALUSelector
);

  ROM #(.dataWidth(4)) HelperROM (.addr({ALUOp, funct}), .data(ALUSelector));

  // Notes on the sheet:
  //   contents of HelperROM (hex, n*v repeats v):
  //   64*0 64*1 9 0 0 0 9 0 a b 18*0 3 7*0 1 0 4 5 6
endmodule

module ALUDecoder (
  input  O5,
  input  O4,
  input  O3,
  input  O2,
  input  O1,
  input  O0,
  output ALUOP1,
  output ALUOP0
);

  wire and_2_out, and_3_out, not_1_out, not_2_out, not_3_out, not_4_out, not_5_out, not_6_out;

  not not_1 (not_1_out, O5);
  not not_2 (not_2_out, O4);
  not not_3 (not_3_out, O3);
  not not_4 (not_4_out, O2);
  not not_5 (not_5_out, O1);
  not not_6 (not_6_out, O0);
  and and_1 (ALUOP1, not_2_out, not_3_out, not_4_out, not_5_out, not_6_out);
  and and_2 (and_2_out, not_1_out, not_2_out, not_3_out, O2, not_5_out, O0);
  and and_3 (and_3_out, not_1_out, not_2_out, O3, not_4_out, O1, not_6_out);
  or or_1 (ALUOP0, and_2_out, and_3_out);
endmodule

module ControlUnit (
  input  [5:0] Opcode,
  input  [5:0] funct,
  input  [5:0] Opcode2,
  input  [5:0] funct2,
  input  [5:0] Opcode3,
  input  [5:0] funct3,
  input  [5:0] Opcode4,
  input  [5:0] funct4,
  input  clk,
  input  rst,
  input  Stall,
  output RegDst,
  output [1:0] ALUop,
  output RegWrite,
  output [1:0] MemToReg,
  output MemWrite,
  output ALUSrc,
  output [1:0] PCSource,
  output Branch,
  output Jal,
  output shiftInst,
  output shiftSRC,
  output StallControl,
  output [1:0] mfhi_mflo,
  output Stall2,
  output Stall3
);

  wire and_1_out, comparator_2_eq, comparator_3_eq, comparator_4_eq, comparator_5_eq, comparator_6_eq,
       comparator_7_eq, comparator_8_eq, comparator_9_eq, comparator_10_eq, comparator_12_eq,
       comparator_13_eq, comparator_14_eq, comparator_15_eq, comparator_16_eq, comparator_19_eq,
       comparator_21_eq, comparator_22_eq, comparator_23_eq, comparator_24_eq, comparator_25_eq,
       comparator_26_eq, not_1_out, or_4_out;

  Comparator #(.width(6)) comparator_1 (.a(Opcode4), .b({6{1'b0}}), .eq(RegDst));  // open: gt, lt
  not not_1 (not_1_out, comparator_2_eq);
  Comparator #(.width(6)) comparator_2 (.a(funct4), .b({6{1'b0}}), .eq(comparator_2_eq));  // open: gt, lt
  Comparator #(.width(6)) comparator_3 (.a(Opcode4), .b({6{1'b0}}), .eq(comparator_3_eq));  // open: gt, lt
  Comparator #(.width(6)) comparator_4 (.a(Opcode4), .b(6'b000011), .eq(comparator_4_eq));  // open: gt, lt
  Comparator #(.width(6)) comparator_5 (.a(Opcode4), .b(6'b100011), .eq(comparator_5_eq));  // open: gt, lt
  Comparator #(.width(6)) comparator_6 (.a(Opcode4), .b(6'b001000), .eq(comparator_6_eq));  // open: gt, lt
  Comparator #(.width(6)) comparator_7 (.a(Opcode4), .b(6'b001010), .eq(comparator_7_eq));  // open: gt, lt
  Comparator #(.width(6)) comparator_8 (.a(Opcode3), .b({6{1'b0}}), .eq(comparator_8_eq));  // open: gt, lt
  Comparator #(.width(6)) comparator_9 (.a(Opcode3), .b(6'b001010), .eq(comparator_9_eq));  // open: gt, lt
  Comparator #(.width(6)) comparator_10 (.a(Opcode3), .b(6'b000011), .eq(comparator_10_eq));  // open: gt, lt
  Comparator #(.width(6)) comparator_11 (.a(Opcode3), .b(6'b101011), .eq(MemWrite));  // open: gt, lt
  Comparator #(.width(6)) comparator_12 (.a(Opcode2), .b(6'b000101), .eq(comparator_12_eq));  // open: gt, lt
  Comparator #(.width(6)) comparator_13 (.a(Opcode), .b(6'b000011), .eq(comparator_13_eq));  // open: gt, lt
  Comparator #(.width(6)) comparator_14 (.a(Opcode), .b(6'b000010), .eq(comparator_14_eq));  // open: gt, lt
  Comparator #(.width(6)) comparator_15 (.a(funct), .b(6'b001000), .eq(comparator_15_eq));  // open: gt, lt
  Comparator #(.width(6)) comparator_16 (.a(Opcode), .b({6{1'b0}}), .eq(comparator_16_eq));  // open: gt, lt
  Comparator #(.width(6)) comparator_17 (.a(Opcode), .b(6'b000101), .eq(Branch));  // open: gt, lt
  Comparator #(.width(6)) comparator_18 (.a(Opcode4), .b(6'b000011), .eq(Jal));  // open: gt, lt
  Comparator #(.width(6)) comparator_19 (.a(Opcode2), .b({6{1'b0}}), .eq(comparator_19_eq));  // open: gt, lt
  and and_1 (and_1_out, not_1_out, comparator_3_eq);
  or or_1 (RegWrite, and_1_out, comparator_4_eq, comparator_5_eq, comparator_6_eq, comparator_7_eq);
  or or_2 (PCSource[0], comparator_13_eq, comparator_14_eq);
  and and_2 (PCSource[1], comparator_15_eq, comparator_16_eq);
  Comparator #(.width(6)) comparator_20 (.a(funct2), .b(6'b000100), .eq(shiftSRC));  // open: gt, lt
  Comparator #(.width(6)) comparator_21 (.a(funct2), .b({6{1'b0}}), .eq(comparator_21_eq));  // open: gt, lt
  Comparator #(.width(6)) comparator_22 (.a(funct3), .b(6'b010010), .eq(comparator_22_eq));  // open: gt, lt
  Comparator #(.width(6)) comparator_23 (.a(Opcode3), .b({6{1'b0}}), .eq(comparator_23_eq));  // open: gt, lt
  Comparator #(.width(6)) comparator_24 (.a(funct3), .b(6'b010000), .eq(comparator_24_eq));  // open: gt, lt
  ALUDecoder ALUDecoder_1 (
    .O5(Opcode2[5]), .O4(Opcode2[4]), .O3(Opcode2[3]), .O2(Opcode2[2]), .O1(Opcode2[1]), .O0(Opcode2[0]),
    .ALUOP1(ALUop[1]), .ALUOP0(ALUop[0]));
  Comparator #(.width(6)) comparator_25 (.a(Opcode3), .b(6'b001000), .eq(comparator_25_eq));  // open: gt, lt
  or or_3 (ALUSrc, comparator_19_eq, comparator_12_eq);
  or or_4 (or_4_out, shiftSRC, comparator_21_eq);
  Comparator #(.width(6)) comparator_26 (.a(funct2), .b(6'b011010), .eq(comparator_26_eq));  // open: gt, lt
  or or_5 (MemToReg[0], comparator_8_eq, comparator_9_eq, comparator_25_eq);
  or or_6 (MemToReg[1], comparator_9_eq, comparator_10_eq);
  and and_3 (shiftInst, or_4_out, comparator_19_eq);
  and and_4 (StallControl, comparator_19_eq, comparator_26_eq);
  and and_5 (mfhi_mflo[0], comparator_22_eq, comparator_23_eq);
  and and_6 (mfhi_mflo[1], comparator_23_eq, comparator_24_eq);
  D_Flip_Flop d_ff_1 (.D(Stall), .clk(clk), .Q(Stall2), .reset(rst));  // open: Qn, preset
  D_Flip_Flop d_ff_2 (.D(Stall2), .clk(clk), .Q(Stall3), .reset(rst));  // open: Qn, preset

  // Other names for the same wires on the sheet: jr = PCSource[1]
endmodule

module IR_and_ID (
  input  [31:0] Instruction,
  input  Stall,
  input  clk,
  input  rst,
  output [31:0] InstructionOut,
  output [25:0] JumpAddress,
  output [5:0] funct,
  output [4:0] shamt,
  output [4:0] rd,
  output [4:0] rt,
  output [4:0] rs,
  output [5:0] opcode,
  output [31:0] SignExt_Imd
);

  wire not_1_out;

  Register #(.width(32)) Instruction_Register (
    .D(Instruction), .en(not_1_out), .clk(clk), .Q({InstructionOut[31:6], funct}), .clr(rst));
  not not_1 (not_1_out, Stall);
  assign SignExt_Imd = {{16{InstructionOut[15]}}, {InstructionOut[15:6], funct}};  // Bit_Extender bit_extender_1

  assign InstructionOut[5:0] = funct;
  assign JumpAddress = {InstructionOut[25:6], funct};
  assign opcode = InstructionOut[31:26];
  assign rd = InstructionOut[15:11];
  assign rs = InstructionOut[25:21];
  assign rt = InstructionOut[20:16];
  assign shamt = InstructionOut[10:6];
endmodule

module InstDoneCircuit (
  input  Stall3,
  input  clk,
  input  rst,
  output InstDone
);

  wire and_1_out, d_ff_1_q, d_ff_2_q, d_ff_3_q, d_ff_4_q, not_1_out, or_1_out;

  D_Flip_Flop d_ff_1 (.D(1'b1), .clk(clk), .Q(d_ff_1_q), .reset(rst));  // open: Qn, preset
  D_Flip_Flop d_ff_2 (.D(d_ff_1_q), .clk(clk), .Q(d_ff_2_q), .reset(rst));  // open: Qn, preset
  D_Flip_Flop d_ff_3 (.D(d_ff_2_q), .clk(clk), .Q(d_ff_3_q), .reset(rst));  // open: Qn, preset
  not not_1 (not_1_out, Stall3);
  and and_1 (and_1_out, d_ff_3_q, not_1_out);
  D_Flip_Flop d_ff_4 (.D(d_ff_3_q), .clk(clk), .Q(d_ff_4_q), .preset(and_1_out), .reset(or_1_out));  // open: Qn
  or or_1 (or_1_out, rst, Stall3);
  D_Flip_Flop d_ff_5 (.D(d_ff_4_q), .clk(clk), .Q(InstDone), .reset(rst));  // open: Qn, preset
endmodule
